# Fritzing sketch Multiboard (saved by Fritzing 0.9.3b)
perfboards: 1

parts:
  Part1 = Arduino Pro Mini (5V)  # not connected
  U1 = LCD-16X2 [package=lcd-16x2]
  RHT1 = Humidity and Temperature Sensor RHT03
  R1 = Rotary Potentiometer (Small) [maximum_resistance=100kΩ package=THT]
  R2 = Resistor [tolerance=±5% resistance=4.7k package=THT]
  J8 = Piezo Speaker
  R3 = Resistor [tolerance=±5% resistance=220 package=THT]
  J9 = female pin header, 12 pins [form="♀ (female)"]
  J10 = female pin header, 12 pins [form="♀ (female)"]
  J7 = female pin header, 4 pins [form="♀ (female)"]
  J11 = female pin header, 2 pins [form="♀ (female)"]
  R4 = Resistor [tolerance=±5% resistance=1k package=THT]  # not connected
  J12 = female pin header, 2 pins [form="♀ (female)"]
  S1 = Pushbutton [package="[THT]"]
  J13 = female pin header, 12 pins [form="♀ (female)"]
  RHT2 = Humidity and Temperature Sensor RHT03  # not connected
  R5 = Resistor [tolerance=±5% resistance=4.7k package=THT]
  IR2 = TSOP312.., 314.. [package=THT]

nets:
  N1: U1.VSS, U1.R_W
  N2: U1.VO, R1.wiper
  N3: U1.RS, J10.pin8
  N4: U1.E, J10.pin6
  N5: U1.DB4, J10.pin5
  N6: U1.DB5, J10.pin4
  N7: U1.DB6, J10.pin3
  N8: U1.DB7, J10.pin1
  N9: U1.A, R3.Pin_1
  N10: RHT1.Vcc, R1.leg2, R2.Pin_0, R3.Pin_0, J7.pin4
  N11: RHT1.Data-signal, J10.pin2, J7.pin3, J13.pin10, R5.Pin_0
  N12: RHT1.GND_1, J7.pin2
  N13: RHT1.GND_2, J7.pin1
  N14: J8.pin1, J11.pin2, J12.pin1, S1.Pin_1, S1.Pin_2
  N15: J8.pin2, J9.pin8
  N16: J9.pin1, J13.pin8, IR2.GND
  N17: J9.pin2, J13.pin2
  N18: J9.pin3, J13.pin3
  N19: J9.pin4, J13.pin4
  N20: J9.pin6, S1.Pin_3, S1.Pin_4
  N21: J9.pin7, J12.pin2
  N22: J9.pin9, J13.pin9
  N23: J9.pin10, J13.pin1
  N24: J11.pin1, J13.pin6
  N25: J13.pin7, IR2.Vs
